# Fritzing sketch Prototype 1 (saved by Fritzing 0.9.3b)
breadboards: 1

parts:
  Part1 = Arduino Nano (Rev3.0)
  Left_Motor = Vibration Motor- ROB-08449 [package=vibe-motor-10mm]
  Right_Motor = Vibration Motor- ROB-08449 [package=vibe-motor-10mm]
  Left_Sensor = hc-sr04
  Right_Sensor = hc-sr04

nets:
  GND: Part1.GND, Left_Motor.+, Right_Motor.+, Left_Sensor.GND, Right_Sensor.GND
  N1: Part1.D6, Right_Sensor.Echo
  N2: Part1.D7, Right_Sensor.Trig
  N3: Part1.D8, Left_Sensor.Echo
  N4: Part1.D9, Left_Sensor.Trig
  VCC: Part1.5V, Left_Sensor.VCC, Right_Sensor.VCC
  N5: Part1.A5, Right_Motor.-
  N6: Part1.A3, Left_Motor.-
